// Logisim project VLSIPROJ.circ as structural Verilog: 4 circuits, main circuit main
module main (
  input  S1,
  input  S0,
  input  in_3,
  input  in_4,
  input  in_5,
  input  in_6,
  input  in_7,
  input  in_8,
  input  in_9,
  input  in_10,
  input  in_11,
  input  in_12,
  input  in_13,
  input  Group_B,
  input  in_15,
  input  in_16,
  input  in_17,
  input  in_18,
  output y0,
  output y1,
  output y2,
  output y3,
  output y4,
  output y5,
  output y6,
  output y7,
  output y8,
  output y9,
  output y10,
  output y11,
  output L_12_3ce61fce,
  output L_13_461d2434,
  output y14,
  output y15
);

  wire l_8bit_fa_defb4cb9_1_cout, l_8bit_fa_defb4cb9_1_y0, l_8bit_fa_defb4cb9_1_y1, l_8bit_fa_defb4cb9_1_y2,
       l_8bit_fa_defb4cb9_1_y3, l_8bit_fa_defb4cb9_1_y4, l_8bit_fa_defb4cb9_1_y5, l_8bit_fa_defb4cb9_1_y6,
       l_8bit_fa_defb4cb9_1_y7, l_8bit_fa_defb4cb9_2_cout, l_8bit_fa_defb4cb9_2_y0, l_8bit_fa_defb4cb9_2_y1,
       l_8bit_fa_defb4cb9_2_y2, l_8bit_fa_defb4cb9_2_y3, l_8bit_fa_defb4cb9_2_y4, l_8bit_fa_defb4cb9_2_y5,
       l_8bit_fa_defb4cb9_2_y6, l_8bit_fa_defb4cb9_2_y7, l_8bit_fa_defb4cb9_3_cout, l_8bit_fa_defb4cb9_3_y0,
       l_8bit_fa_defb4cb9_3_y1, l_8bit_fa_defb4cb9_3_y2, l_8bit_fa_defb4cb9_3_y3, l_8bit_fa_defb4cb9_3_y4,
       l_8bit_fa_defb4cb9_3_y5, l_8bit_fa_defb4cb9_3_y6, l_8bit_fa_defb4cb9_3_y7, main_1_y0, main_1_y1,
       main_1_y2, main_1_y3, main_1_y4, main_1_y5, main_1_y6, main_1_y7, main_1_y8, main_1_y9, main_1_y10,
       main_1_y11, main_1_y12, main_1_y13, main_1_y14, main_1_y15, not_1_out, shiftadd_1_p3, shiftadd_1_p4,
       shiftadd_1_p5, shiftadd_1_p6, shiftadd_1_p7, shiftadd_1_p8, shiftadd_1_p9, shiftadd_1_p10,
       shiftadd_1_p11, shiftadd_1_p12, shiftadd_1_p13, shiftadd_1_p14, shiftadd_1_p15, shiftadd_1_p17,
       shiftadd_1_p18;

  not not_1 (not_1_out, S0);
  // Shiftadd shiftadd_1: pin names not known; wires that end beside it: {in_10, in_9, in_8, in_7, in_6, in_5, in_4, in_3}, {in_18, in_17, in_16, in_15, Group_B, in_13, in_12, in_11}, shiftadd_1_p3, shiftadd_1_p4, shiftadd_1_p5, shiftadd_1_p6, shiftadd_1_p7, shiftadd_1_p8, shiftadd_1_p9, shiftadd_1_p10, shiftadd_1_p11, shiftadd_1_p12, shiftadd_1_p13, shiftadd_1_p14, shiftadd_1_p15, 1'b0, shiftadd_1_p17, shiftadd_1_p18
  L_8bit_FA_defb4cb9 l_8bit_fa_defb4cb9_1 (
    .a0(in_3), .add_sub_e356f4c1(not_1_out), .b7(in_18), .a7(in_10), .b6(in_17), .a6(in_9), .b5(in_16),
    .a5(in_8), .b4(in_15), .a4(in_7), .b3(Group_B), .a3(in_6), .b2(in_13), .a2(in_5), .b1(in_12), .a1(in_4),
    .b0(in_11), .y0(l_8bit_fa_defb4cb9_1_y0), .cout(l_8bit_fa_defb4cb9_1_cout), .y7(l_8bit_fa_defb4cb9_1_y7),
    .y6(l_8bit_fa_defb4cb9_1_y6), .y5(l_8bit_fa_defb4cb9_1_y5), .y4(l_8bit_fa_defb4cb9_1_y4),
    .y3(l_8bit_fa_defb4cb9_1_y3), .y2(l_8bit_fa_defb4cb9_1_y2), .y1(l_8bit_fa_defb4cb9_1_y1));
  CSA_and_CPA_main main_1 (
    .A({in_18, in_17, in_16, in_15, Group_B, in_13, in_12, in_11}),
    .B({in_10, in_9, in_8, in_7, in_6, in_5, in_4, in_3}), .Y15(main_1_y15), .Y14(main_1_y14),
    .Y13(main_1_y13), .Y12(main_1_y12), .Y11(main_1_y11), .Y10(main_1_y10), .Y9(main_1_y9), .Y8(main_1_y8),
    .Y7(main_1_y7), .Y6(main_1_y6), .Y5(main_1_y5), .Y4(main_1_y4), .Y3(main_1_y3), .Y2(main_1_y2),
    .Y1(main_1_y1), .Y0(main_1_y0));
  L_8bit_FA_defb4cb9 l_8bit_fa_defb4cb9_2 (
    .a0(l_8bit_fa_defb4cb9_1_y1), .add_sub_e356f4c1(1'b0), .b7(1'b0), .a7(1'b0), .b6(1'b0),
    .a6(l_8bit_fa_defb4cb9_1_y7), .b5(1'b0), .a5(l_8bit_fa_defb4cb9_1_y6), .b4(1'b0),
    .a4(l_8bit_fa_defb4cb9_1_y5), .b3(1'b0), .a3(l_8bit_fa_defb4cb9_1_y4), .b2(1'b0),
    .a2(l_8bit_fa_defb4cb9_1_y3), .b1(1'b0), .a1(l_8bit_fa_defb4cb9_1_y2), .b0(1'b0),
    .y0(l_8bit_fa_defb4cb9_2_y0), .cout(l_8bit_fa_defb4cb9_2_cout), .y7(l_8bit_fa_defb4cb9_2_y7),
    .y6(l_8bit_fa_defb4cb9_2_y6), .y5(l_8bit_fa_defb4cb9_2_y5), .y4(l_8bit_fa_defb4cb9_2_y4),
    .y3(l_8bit_fa_defb4cb9_2_y3), .y2(l_8bit_fa_defb4cb9_2_y2), .y1(l_8bit_fa_defb4cb9_2_y1));
  L_8bit_FA_defb4cb9 l_8bit_fa_defb4cb9_3 (
    .a0(l_8bit_fa_defb4cb9_2_y1), .add_sub_e356f4c1(1'b0), .b7(l_8bit_fa_defb4cb9_1_y7),
    .a7(l_8bit_fa_defb4cb9_2_cout), .b6(l_8bit_fa_defb4cb9_1_y6), .a6(l_8bit_fa_defb4cb9_2_y7),
    .b5(l_8bit_fa_defb4cb9_1_y5), .a5(l_8bit_fa_defb4cb9_2_y6), .b4(l_8bit_fa_defb4cb9_1_y4),
    .a4(l_8bit_fa_defb4cb9_2_y5), .b3(l_8bit_fa_defb4cb9_1_y3), .a3(l_8bit_fa_defb4cb9_2_y4),
    .b2(l_8bit_fa_defb4cb9_1_y2), .a2(l_8bit_fa_defb4cb9_2_y3), .b1(l_8bit_fa_defb4cb9_1_y1),
    .a1(l_8bit_fa_defb4cb9_2_y2), .b0(l_8bit_fa_defb4cb9_1_y0), .y0(l_8bit_fa_defb4cb9_3_y0),
    .cout(l_8bit_fa_defb4cb9_3_cout), .y7(l_8bit_fa_defb4cb9_3_y7), .y6(l_8bit_fa_defb4cb9_3_y6),
    .y5(l_8bit_fa_defb4cb9_3_y5), .y4(l_8bit_fa_defb4cb9_3_y4), .y3(l_8bit_fa_defb4cb9_3_y3),
    .y2(l_8bit_fa_defb4cb9_3_y2), .y1(l_8bit_fa_defb4cb9_3_y1));
  L_4_1MUX_5f0cd658 l_4_1mux_5f0cd658_1 (
    .MUL_SA_e87f8820(shiftadd_1_p3), .sub(l_8bit_fa_defb4cb9_1_y0), .ADD(l_8bit_fa_defb4cb9_1_y0),
    .CSA_CPA_MUL_d43ffa23(main_1_y0), .s0(S0), .s1(S1), .y(y0));
  L_4_1MUX_5f0cd658 l_4_1mux_5f0cd658_2 (
    .MUL_SA_e87f8820(shiftadd_1_p4), .sub(l_8bit_fa_defb4cb9_1_y1), .ADD(l_8bit_fa_defb4cb9_2_y0),
    .CSA_CPA_MUL_d43ffa23(main_1_y1), .s0(S0), .s1(S1), .y(y1));
  L_4_1MUX_5f0cd658 l_4_1mux_5f0cd658_3 (
    .MUL_SA_e87f8820(shiftadd_1_p5), .sub(l_8bit_fa_defb4cb9_1_y2), .ADD(l_8bit_fa_defb4cb9_3_y0),
    .CSA_CPA_MUL_d43ffa23(main_1_y2), .s0(S0), .s1(S1), .y(y2));
  L_4_1MUX_5f0cd658 l_4_1mux_5f0cd658_4 (
    .MUL_SA_e87f8820(shiftadd_1_p7), .sub(l_8bit_fa_defb4cb9_1_y4), .ADD(l_8bit_fa_defb4cb9_3_y2),
    .CSA_CPA_MUL_d43ffa23(main_1_y4), .s0(S0), .s1(S1), .y(y4));
  L_4_1MUX_5f0cd658 l_4_1mux_5f0cd658_5 (
    .MUL_SA_e87f8820(shiftadd_1_p8), .sub(l_8bit_fa_defb4cb9_1_y5), .ADD(l_8bit_fa_defb4cb9_3_y3),
    .CSA_CPA_MUL_d43ffa23(main_1_y5), .s0(S0), .s1(S1), .y(y5));
  L_4_1MUX_5f0cd658 l_4_1mux_5f0cd658_6 (
    .MUL_SA_e87f8820(shiftadd_1_p9), .sub(l_8bit_fa_defb4cb9_1_y6), .ADD(l_8bit_fa_defb4cb9_3_y4),
    .CSA_CPA_MUL_d43ffa23(main_1_y6), .s0(S0), .s1(S1), .y(y6));
  L_4_1MUX_5f0cd658 l_4_1mux_5f0cd658_7 (
    .MUL_SA_e87f8820(shiftadd_1_p10), .sub(l_8bit_fa_defb4cb9_1_y7), .ADD(l_8bit_fa_defb4cb9_3_y5),
    .CSA_CPA_MUL_d43ffa23(main_1_y7), .s0(S0), .s1(S1), .y(y7));
  L_4_1MUX_5f0cd658 l_4_1mux_5f0cd658_8 (
    .MUL_SA_e87f8820(shiftadd_1_p11), .sub(1'b0), .ADD(l_8bit_fa_defb4cb9_3_y6),
    .CSA_CPA_MUL_d43ffa23(main_1_y8), .s0(S0), .s1(S1), .y(y8));
  L_4_1MUX_5f0cd658 l_4_1mux_5f0cd658_9 (
    .MUL_SA_e87f8820(shiftadd_1_p12), .sub(1'b0), .ADD(l_8bit_fa_defb4cb9_3_y7),
    .CSA_CPA_MUL_d43ffa23(main_1_y9), .s0(S0), .s1(S1), .y(y9));
  L_4_1MUX_5f0cd658 l_4_1mux_5f0cd658_10 (
    .MUL_SA_e87f8820(shiftadd_1_p13), .sub(1'b0), .ADD(l_8bit_fa_defb4cb9_3_cout),
    .CSA_CPA_MUL_d43ffa23(main_1_y10), .s0(S0), .s1(S1), .y(y10));
  L_4_1MUX_5f0cd658 l_4_1mux_5f0cd658_11 (
    .MUL_SA_e87f8820(shiftadd_1_p14), .sub(1'b0), .ADD(1'b0), .CSA_CPA_MUL_d43ffa23(main_1_y11), .s0(S0),
    .s1(S1), .y(y11));
  L_4_1MUX_5f0cd658 l_4_1mux_5f0cd658_12 (
    .MUL_SA_e87f8820(shiftadd_1_p15), .sub(1'b0), .ADD(1'b0), .CSA_CPA_MUL_d43ffa23(main_1_y12), .s0(S0),
    .s1(S1), .y(L_12_3ce61fce));
  L_4_1MUX_5f0cd658 l_4_1mux_5f0cd658_13 (
    .MUL_SA_e87f8820(1'b0), .sub(1'b0), .ADD(1'b0), .CSA_CPA_MUL_d43ffa23(main_1_y13), .s0(S0), .s1(S1),
    .y(L_13_461d2434));
  L_4_1MUX_5f0cd658 l_4_1mux_5f0cd658_14 (
    .MUL_SA_e87f8820(shiftadd_1_p17), .sub(1'b0), .ADD(1'b0), .CSA_CPA_MUL_d43ffa23(main_1_y14), .s0(S0),
    .s1(S1), .y(y14));
  L_4_1MUX_5f0cd658 l_4_1mux_5f0cd658_15 (
    .MUL_SA_e87f8820(shiftadd_1_p18), .sub(1'b0), .ADD(1'b0), .CSA_CPA_MUL_d43ffa23(main_1_y15), .s0(S0),
    .s1(S1), .y(y15));
  L_4_1MUX_5f0cd658 l_4_1mux_5f0cd658_16 (
    .MUL_SA_e87f8820(shiftadd_1_p6), .sub(l_8bit_fa_defb4cb9_1_y3), .ADD(l_8bit_fa_defb4cb9_3_y1),
    .CSA_CPA_MUL_d43ffa23(main_1_y3), .s0(S0), .s1(S1), .y(y3));
  LED Cout_SUB_cf407f75 (.in(l_8bit_fa_defb4cb9_1_cout));

  // Notes on the sheet:
  //   Group A
endmodule

module L_1bit_FA_4ff9fd07 (
  input  a,
  input  b,
  input  cin,
  output sum,
  output cout
);

  wire and_1_out, and_2_out, xor_1_out;

  xor xor_1 (xor_1_out, a, b);
  xor xor_2 (sum, xor_1_out, cin);
  and and_1 (and_1_out, xor_1_out, cin);
  or or_1 (cout, and_1_out, and_2_out);
  and and_2 (and_2_out, a, b);
endmodule

module L_8bit_FA_defb4cb9 (
  input  add_sub_e356f4c1,
  input  b7,
  input  a7,
  input  b6,
  input  a6,
  input  b5,
  input  a5,
  input  b4,
  input  a4,
  input  b3,
  input  a3,
  input  b2,
  input  a2,
  input  b1,
  input  a1,
  input  b0,
  input  a0,
  output cout,
  output y7,
  output y6,
  output y5,
  output y4,
  output y3,
  output y2,
  output y1,
  output y0
);

  wire l_1bit_fa_4ff9fd07_2_cout, l_1bit_fa_4ff9fd07_3_cout, l_1bit_fa_4ff9fd07_4_cout,
       l_1bit_fa_4ff9fd07_5_cout, l_1bit_fa_4ff9fd07_6_cout, l_1bit_fa_4ff9fd07_7_cout,
       l_1bit_fa_4ff9fd07_8_cout, xor_1_out, xor_2_out, xor_3_out, xor_4_out, xor_5_out, xor_6_out,
       xor_7_out, xor_8_out;

  xor xor_1 (xor_1_out, b7, add_sub_e356f4c1);
  L_1bit_FA_4ff9fd07 l_1bit_fa_4ff9fd07_1 (
    .cin(l_1bit_fa_4ff9fd07_2_cout), .a(a7), .b(xor_1_out), .sum(y7), .cout(cout));
  xor xor_2 (xor_2_out, b6, add_sub_e356f4c1);
  L_1bit_FA_4ff9fd07 l_1bit_fa_4ff9fd07_2 (
    .cin(l_1bit_fa_4ff9fd07_3_cout), .a(a6), .b(xor_2_out), .sum(y6), .cout(l_1bit_fa_4ff9fd07_2_cout));
  xor xor_3 (xor_3_out, b5, add_sub_e356f4c1);
  L_1bit_FA_4ff9fd07 l_1bit_fa_4ff9fd07_3 (
    .cin(l_1bit_fa_4ff9fd07_4_cout), .a(a5), .b(xor_3_out), .sum(y5), .cout(l_1bit_fa_4ff9fd07_3_cout));
  xor xor_4 (xor_4_out, b4, add_sub_e356f4c1);
  L_1bit_FA_4ff9fd07 l_1bit_fa_4ff9fd07_4 (
    .cin(l_1bit_fa_4ff9fd07_5_cout), .a(a4), .b(xor_4_out), .sum(y4), .cout(l_1bit_fa_4ff9fd07_4_cout));
  xor xor_5 (xor_5_out, b3, add_sub_e356f4c1);
  L_1bit_FA_4ff9fd07 l_1bit_fa_4ff9fd07_5 (
    .cin(l_1bit_fa_4ff9fd07_6_cout), .a(a3), .b(xor_5_out), .sum(y3), .cout(l_1bit_fa_4ff9fd07_5_cout));
  xor xor_6 (xor_6_out, b2, add_sub_e356f4c1);
  L_1bit_FA_4ff9fd07 l_1bit_fa_4ff9fd07_6 (
    .cin(l_1bit_fa_4ff9fd07_7_cout), .a(a2), .b(xor_6_out), .sum(y2), .cout(l_1bit_fa_4ff9fd07_6_cout));
  xor xor_7 (xor_7_out, b1, add_sub_e356f4c1);
  L_1bit_FA_4ff9fd07 l_1bit_fa_4ff9fd07_7 (
    .cin(l_1bit_fa_4ff9fd07_8_cout), .a(a1), .b(xor_7_out), .sum(y1), .cout(l_1bit_fa_4ff9fd07_7_cout));
  xor xor_8 (xor_8_out, b0, add_sub_e356f4c1);
  L_1bit_FA_4ff9fd07 l_1bit_fa_4ff9fd07_8 (
    .cin(add_sub_e356f4c1), .a(a0), .b(xor_8_out), .sum(y0), .cout(l_1bit_fa_4ff9fd07_8_cout));
endmodule

module L_4_1MUX_5f0cd658 (
  input  CSA_CPA_MUL_d43ffa23,
  input  MUL_SA_e87f8820,
  input  sub,
  input  ADD,
  input  s0,
  input  s1,
  output y
);

  wire multiplexer_1_out, multiplexer_2_out;

  Multiplexer #(.enable("true")) multiplexer_1 (
    .in0(CSA_CPA_MUL_d43ffa23), .in1(MUL_SA_e87f8820), .out(multiplexer_1_out), .sel(s0), .en(1'b1));
  Multiplexer #(.enable("true")) multiplexer_2 (.in0(sub), .in1(ADD), .out(multiplexer_2_out), .sel(s0), .en(1'b1));
  Multiplexer #(.enable("true")) multiplexer_3 (
    .in0(multiplexer_1_out), .in1(multiplexer_2_out), .out(y), .sel(s1), .en(1'b1));
endmodule
