// Logisim project csa.circ as structural Verilog: 1 circuit, main circuit main
module main (
  input  [7:0] A,
  input  [7:0] B,
  output [15:0] Y
);

  wire adder_1_cout, adder_2_cout, adder_2_out, adder_3_cout, adder_3_out, adder_4_cout, adder_4_out,
       adder_5_cout, adder_5_out, adder_6_cout, adder_6_out, adder_7_cout, adder_7_out, adder_8_cout,
       adder_9_cout, adder_9_out, adder_10_cout, adder_10_out, adder_11_cout, adder_11_out, adder_12_cout,
       adder_12_out, adder_13_cout, adder_13_out, adder_14_cout, adder_14_out, adder_15_cout, adder_16_cout,
       adder_16_out, adder_17_cout, adder_17_out, adder_18_cout, adder_18_out, adder_19_cout, adder_19_out,
       adder_20_cout, adder_20_out, adder_21_cout, adder_21_out, adder_22_cout, adder_23_cout, adder_23_out,
       adder_24_cout, adder_24_out, adder_25_cout, adder_25_out, adder_26_cout, adder_26_out, adder_27_cout,
       adder_27_out, adder_28_cout, adder_28_out, adder_29_cout, adder_30_cout, adder_30_out, adder_31_cout,
       adder_31_out, adder_32_cout, adder_32_out, adder_33_cout, adder_33_out, adder_34_cout, adder_34_out,
       adder_35_cout, adder_35_out, adder_36_cout, adder_37_cout, adder_37_out, adder_38_cout, adder_38_out,
       adder_39_cout, adder_39_out, adder_40_cout, adder_40_out, adder_41_cout, adder_41_out, adder_42_cout,
       adder_42_out, adder_43_cout, adder_44_cout, adder_44_out, adder_45_cout, adder_45_out, adder_46_cout,
       adder_46_out, adder_47_cout, adder_47_out, adder_48_cout, adder_48_out, adder_49_cout, adder_49_out,
       adder_50_cout, adder_51_cout, adder_52_cout, adder_53_cout, adder_54_cout, adder_55_cout, and_2_out,
       and_3_out, and_4_out, and_5_out, and_6_out, and_7_out, and_8_out, and_9_out, and_10_out, and_11_out,
       and_12_out, and_13_out, and_14_out, and_15_out, and_16_out, and_17_out, and_18_out, and_19_out,
       and_20_out, and_21_out, and_22_out, and_23_out, and_24_out, and_25_out, and_26_out, and_27_out,
       and_28_out, and_29_out, and_30_out, and_31_out, and_32_out, and_33_out, and_34_out, and_35_out,
       and_36_out, and_37_out, and_38_out, and_39_out, and_40_out, and_41_out, and_42_out, and_43_out,
       and_44_out, and_45_out, and_46_out, and_47_out, and_48_out, and_49_out, and_50_out, and_51_out,
       and_52_out, and_53_out, and_54_out, and_55_out, and_56_out, and_57_out, and_58_out, and_59_out,
       and_60_out, and_61_out, and_62_out, and_63_out, and_64_out;

  and and_1 (Y[0], A[0], B[0]);
  and and_2 (and_2_out, A[0], B[1]);
  and and_3 (and_3_out, A[1], B[0]);
  and and_4 (and_4_out, A[0], B[3]);
  and and_5 (and_5_out, A[1], B[2]);
  and and_6 (and_6_out, A[0], B[5]);
  and and_7 (and_7_out, A[1], B[4]);
  and and_8 (and_8_out, A[0], B[7]);
  and and_9 (and_9_out, A[1], B[6]);
  Adder #(.width(1)) adder_1 (.a(and_2_out), .b(and_3_out), .out(Y[1]), .cin(1'b0), .cout(adder_1_cout));
  and and_10 (and_10_out, A[0], B[2]);
  Adder #(.width(1)) adder_2 (.a(and_10_out), .b(and_11_out), .out(adder_2_out), .cin(1'b0), .cout(adder_2_cout));
  and and_11 (and_11_out, A[1], B[1]);
  Adder #(.width(1)) adder_3 (.a(and_4_out), .b(and_5_out), .out(adder_3_out), .cin(1'b0), .cout(adder_3_cout));
  and and_12 (and_12_out, A[0], B[4]);
  Adder #(.width(1)) adder_4 (.a(and_12_out), .b(and_13_out), .out(adder_4_out), .cin(1'b0), .cout(adder_4_cout));
  and and_13 (and_13_out, A[1], B[3]);
  Adder #(.width(1)) adder_5 (.a(and_6_out), .b(and_7_out), .out(adder_5_out), .cin(1'b0), .cout(adder_5_cout));
  and and_14 (and_14_out, A[0], B[6]);
  Adder #(.width(1)) adder_6 (.a(and_14_out), .b(and_15_out), .out(adder_6_out), .cin(1'b0), .cout(adder_6_cout));
  and and_15 (and_15_out, A[1], B[5]);
  Adder #(.width(1)) adder_7 (.a(and_8_out), .b(and_9_out), .out(adder_7_out), .cin(1'b0), .cout(adder_7_cout));
  and and_16 (and_16_out, A[1], B[7]);
  and and_17 (and_17_out, A[2], B[0]);
  and and_18 (and_18_out, A[2], B[1]);
  and and_19 (and_19_out, A[2], B[2]);
  and and_20 (and_20_out, A[2], B[3]);
  and and_21 (and_21_out, A[2], B[4]);
  and and_22 (and_22_out, A[2], B[5]);
  and and_23 (and_23_out, A[2], B[6]);
  and and_24 (and_24_out, A[2], B[7]);
  Adder #(.width(1)) adder_8 (.a(adder_2_out), .b(and_17_out), .out(Y[2]), .cin(adder_1_cout), .cout(adder_8_cout));
  Adder #(.width(1)) adder_9 (
    .a(adder_3_out), .b(and_18_out), .out(adder_9_out), .cin(adder_2_cout), .cout(adder_9_cout));
  Adder #(.width(1)) adder_10 (
    .a(adder_4_out), .b(and_19_out), .out(adder_10_out), .cin(adder_3_cout), .cout(adder_10_cout));
  Adder #(.width(1)) adder_11 (
    .a(adder_5_out), .b(and_20_out), .out(adder_11_out), .cin(adder_4_cout), .cout(adder_11_cout));
  Adder #(.width(1)) adder_12 (
    .a(adder_6_out), .b(and_21_out), .out(adder_12_out), .cin(adder_5_cout), .cout(adder_12_cout));
  Adder #(.width(1)) adder_13 (
    .a(adder_7_out), .b(and_22_out), .out(adder_13_out), .cin(adder_6_cout), .cout(adder_13_cout));
  Adder #(.width(1)) adder_14 (
    .a(and_16_out), .b(and_23_out), .out(adder_14_out), .cin(adder_7_cout), .cout(adder_14_cout));
  and and_25 (and_25_out, A[3], B[0]);
  and and_26 (and_26_out, A[3], B[1]);
  and and_27 (and_27_out, A[3], B[2]);
  and and_28 (and_28_out, A[3], B[3]);
  and and_29 (and_29_out, A[3], B[4]);
  and and_30 (and_30_out, A[3], B[5]);
  and and_31 (and_31_out, A[3], B[6]);
  and and_32 (and_32_out, A[3], B[7]);
  Adder #(.width(1)) adder_15 (.a(adder_9_out), .b(and_25_out), .out(Y[3]), .cin(adder_8_cout), .cout(adder_15_cout));
  Adder #(.width(1)) adder_16 (
    .a(adder_10_out), .b(and_26_out), .out(adder_16_out), .cin(adder_9_cout), .cout(adder_16_cout));
  Adder #(.width(1)) adder_17 (
    .a(adder_11_out), .b(and_27_out), .out(adder_17_out), .cin(adder_10_cout), .cout(adder_17_cout));
  Adder #(.width(1)) adder_18 (
    .a(adder_12_out), .b(and_28_out), .out(adder_18_out), .cin(adder_11_cout), .cout(adder_18_cout));
  Adder #(.width(1)) adder_19 (
    .a(adder_13_out), .b(and_29_out), .out(adder_19_out), .cin(adder_12_cout), .cout(adder_19_cout));
  Adder #(.width(1)) adder_20 (
    .a(adder_14_out), .b(and_30_out), .out(adder_20_out), .cin(adder_13_cout), .cout(adder_20_cout));
  Adder #(.width(1)) adder_21 (
    .a(and_24_out), .b(and_31_out), .out(adder_21_out), .cin(adder_14_cout), .cout(adder_21_cout));
  Adder #(.width(1)) adder_22 (.a(adder_16_out), .b(and_33_out), .out(Y[4]), .cin(adder_15_cout), .cout(adder_22_cout));
  and and_33 (and_33_out, A[4], B[0]);
  Adder #(.width(1)) adder_23 (
    .a(adder_17_out), .b(and_34_out), .out(adder_23_out), .cin(adder_16_cout), .cout(adder_23_cout));
  and and_34 (and_34_out, A[4], B[1]);
  Adder #(.width(1)) adder_24 (
    .a(adder_18_out), .b(and_35_out), .out(adder_24_out), .cin(adder_17_cout), .cout(adder_24_cout));
  and and_35 (and_35_out, A[4], B[2]);
  Adder #(.width(1)) adder_25 (
    .a(adder_19_out), .b(and_36_out), .out(adder_25_out), .cin(adder_18_cout), .cout(adder_25_cout));
  and and_36 (and_36_out, A[4], B[3]);
  Adder #(.width(1)) adder_26 (
    .a(adder_20_out), .b(and_37_out), .out(adder_26_out), .cin(adder_19_cout), .cout(adder_26_cout));
  and and_37 (and_37_out, A[4], B[4]);
  Adder #(.width(1)) adder_27 (
    .a(adder_21_out), .b(and_38_out), .out(adder_27_out), .cin(adder_20_cout), .cout(adder_27_cout));
  and and_38 (and_38_out, A[4], B[5]);
  Adder #(.width(1)) adder_28 (
    .a(and_32_out), .b(and_39_out), .out(adder_28_out), .cin(adder_21_cout), .cout(adder_28_cout));
  and and_39 (and_39_out, A[4], B[6]);
  and and_40 (and_40_out, A[4], B[7]);
  and and_41 (and_41_out, A[5], B[0]);
  and and_42 (and_42_out, A[5], B[1]);
  and and_43 (and_43_out, A[5], B[2]);
  and and_44 (and_44_out, A[5], B[3]);
  and and_45 (and_45_out, A[5], B[4]);
  and and_46 (and_46_out, A[5], B[5]);
  and and_47 (and_47_out, A[5], B[6]);
  and and_48 (and_48_out, A[5], B[7]);
  Adder #(.width(1)) adder_29 (.a(adder_23_out), .b(and_41_out), .out(Y[5]), .cin(adder_22_cout), .cout(adder_29_cout));
  Adder #(.width(1)) adder_30 (
    .a(adder_24_out), .b(and_42_out), .out(adder_30_out), .cin(adder_23_cout), .cout(adder_30_cout));
  Adder #(.width(1)) adder_31 (
    .a(adder_25_out), .b(and_43_out), .out(adder_31_out), .cin(adder_24_cout), .cout(adder_31_cout));
  Adder #(.width(1)) adder_32 (
    .a(adder_26_out), .b(and_44_out), .out(adder_32_out), .cin(adder_25_cout), .cout(adder_32_cout));
  Adder #(.width(1)) adder_33 (
    .a(adder_27_out), .b(and_45_out), .out(adder_33_out), .cin(adder_26_cout), .cout(adder_33_cout));
  Adder #(.width(1)) adder_34 (
    .a(adder_28_out), .b(and_46_out), .out(adder_34_out), .cin(adder_27_cout), .cout(adder_34_cout));
  Adder #(.width(1)) adder_35 (
    .a(and_40_out), .b(and_47_out), .out(adder_35_out), .cin(adder_28_cout), .cout(adder_35_cout));
  and and_49 (and_49_out, A[6], B[0]);
  and and_50 (and_50_out, A[6], B[1]);
  and and_51 (and_51_out, A[6], B[2]);
  and and_52 (and_52_out, A[6], B[3]);
  and and_53 (and_53_out, A[6], B[4]);
  and and_54 (and_54_out, A[6], B[5]);
  and and_55 (and_55_out, A[6], B[6]);
  and and_56 (and_56_out, A[6], B[7]);
  Adder #(.width(1)) adder_36 (.a(adder_30_out), .b(and_49_out), .out(Y[6]), .cin(adder_29_cout), .cout(adder_36_cout));
  Adder #(.width(1)) adder_37 (
    .a(adder_31_out), .b(and_50_out), .out(adder_37_out), .cin(adder_30_cout), .cout(adder_37_cout));
  Adder #(.width(1)) adder_38 (
    .a(adder_32_out), .b(and_51_out), .out(adder_38_out), .cin(adder_31_cout), .cout(adder_38_cout));
  Adder #(.width(1)) adder_39 (
    .a(adder_33_out), .b(and_52_out), .out(adder_39_out), .cin(adder_32_cout), .cout(adder_39_cout));
  Adder #(.width(1)) adder_40 (
    .a(adder_34_out), .b(and_53_out), .out(adder_40_out), .cin(adder_33_cout), .cout(adder_40_cout));
  Adder #(.width(1)) adder_41 (
    .a(adder_35_out), .b(and_54_out), .out(adder_41_out), .cin(adder_34_cout), .cout(adder_41_cout));
  Adder #(.width(1)) adder_42 (
    .a(and_48_out), .b(and_55_out), .out(adder_42_out), .cin(adder_35_cout), .cout(adder_42_cout));
  and and_57 (and_57_out, A[7], B[0]);
  and and_58 (and_58_out, A[7], B[1]);
  and and_59 (and_59_out, A[7], B[2]);
  and and_60 (and_60_out, A[7], B[3]);
  and and_61 (and_61_out, A[7], B[4]);
  and and_62 (and_62_out, A[7], B[5]);
  and and_63 (and_63_out, A[7], B[6]);
  and and_64 (and_64_out, A[7], B[7]);
  Adder #(.width(1)) adder_43 (.a(adder_37_out), .b(and_57_out), .out(Y[7]), .cin(adder_36_cout), .cout(adder_43_cout));
  Adder #(.width(1)) adder_44 (
    .a(adder_38_out), .b(and_58_out), .out(adder_44_out), .cin(adder_37_cout), .cout(adder_44_cout));
  Adder #(.width(1)) adder_45 (
    .a(adder_39_out), .b(and_59_out), .out(adder_45_out), .cin(adder_38_cout), .cout(adder_45_cout));
  Adder #(.width(1)) adder_46 (
    .a(adder_40_out), .b(and_60_out), .out(adder_46_out), .cin(adder_39_cout), .cout(adder_46_cout));
  Adder #(.width(1)) adder_47 (
    .a(adder_41_out), .b(and_61_out), .out(adder_47_out), .cin(adder_40_cout), .cout(adder_47_cout));
  Adder #(.width(1)) adder_48 (
    .a(adder_42_out), .b(and_62_out), .out(adder_48_out), .cin(adder_41_cout), .cout(adder_48_cout));
  Adder #(.width(1)) adder_49 (
    .a(and_56_out), .b(and_63_out), .out(adder_49_out), .cin(adder_42_cout), .cout(adder_49_cout));
  Adder #(.width(1)) adder_50 (.a(adder_43_cout), .b(adder_44_out), .out(Y[8]), .cin(1'b0), .cout(adder_50_cout));
  Adder #(.width(1)) adder_51 (
    .a(adder_44_cout), .b(adder_45_out), .out(Y[9]), .cin(adder_50_cout), .cout(adder_51_cout));
  Adder #(.width(1)) adder_52 (
    .a(adder_45_cout), .b(adder_46_out), .out(Y[10]), .cin(adder_51_cout), .cout(adder_52_cout));
  Adder #(.width(1)) adder_53 (
    .a(adder_46_cout), .b(adder_47_out), .out(Y[11]), .cin(adder_52_cout), .cout(adder_53_cout));
  Adder #(.width(1)) adder_54 (
    .a(adder_47_cout), .b(adder_48_out), .out(Y[12]), .cin(adder_53_cout), .cout(adder_54_cout));
  Adder #(.width(1)) adder_55 (
    .a(adder_48_cout), .b(adder_49_out), .out(Y[13]), .cin(adder_54_cout), .cout(adder_55_cout));
  Adder #(.width(1)) adder_56 (.a(adder_49_cout), .b(and_64_out), .out(Y[14]), .cin(adder_55_cout), .cout(Y[15]));

  // Notes on the sheet:
  //   B0-7
  //   A1
  //   A1
  //   Y7
  //   A0
  //   A2
  //   B0-7
  //   A2
  //   Y7
  //   A3
  //   B0-7
  //   GND
  //   A3
  //   Y7
  //   A4
  //   B0-7
  //   A4
  //   Y7
  //   A5
  //   B0-7
  //   A5
  //   Y7
  //   A6
  //   B0-7
  //   A6
  //   Y7
  //   A7
  //   B0-7
  //   A7
  //   Y7
  //   Y14
  //   Y15
  //   Y1
  //   Y2
  //   Y3
  //   Y4
  //   Y5
  //   Y6
  //   Y7
  //   Y8
  //   Y9
  //   Y10
  //   Y11
  //   Y12
  //   Y13
  //   Y0
endmodule
